# Fritzing sketch IO Breakout (saved by Fritzing 0.9.3b)
circuit board: 3.99442cm x 6.7032cm
breadboards: 1

parts:
  J1 = double row female pin header, 12 pins [form="♀ (female)"]
  J2 = screw terminal, 3 pins
  J3 = screw terminal, 3 pins
  J4 = screw terminal, 6 pins
  J5 = male pin header, 2 pins [form="♂ (male)"]
  J6 = Screw terminal - 2 pins [package=THT]
  IC1 = ULN2803A [package=THT]
  J7 = screw terminal, 8 pins
  C1 = Ceramic Capacitor [capacitance=0.1mF package="100 mil [THT, multilayer]"]

nets:
  N1: J1.pin1, J2.pin1, IC1.0V, C1.1
  N2: J1.pin2, J4.pin2
  N3: J1.pin3, J4.pin1
  N4: J1.pin4, J3.pin3, IC1.In_1, IC1.In_2, IC1.In_3, IC1.In_4, IC1.In_5, IC1.In_6, IC1.In_7, IC1.In_8
  N5: J1.pin5, J3.pin2
  N6: J1.pin6, J3.pin1
  N7: J1.pin7, J4.pin6
  N8: J1.pin8, J4.pin5
  N9: J1.pin9, J4.pin4
  N10: J1.pin10, J4.pin3
  N11: J1.pin11, J2.pin3, IC1.COM_-_Common, C1.0
  N12: J1.pin12, J2.pin2
  N13: J5.pin1, J6.pin2
  N14: J5.pin2, J6.pin1
  N15: IC1.Out_8, J7.pin8
  N16: IC1.Out_7, J7.pin7
  N17: IC1.Out_6, J7.pin6
  N18: IC1.Out_5, J7.pin5
  N19: IC1.Out_4, J7.pin4
  N20: IC1.Out_3, J7.pin3
  N21: IC1.Out_2, J7.pin2
  N22: IC1.Out_1, J7.pin1

notes:
  Gnd
  +3.3V
  +5V
  FAB 001002 ASSY 001002
  CyGate4 I/O Break-out Rev 1.1
  RST
  DIO3
  DIO4
  DIO1
  DIO2
  DIO5
  DIO6
  DIO7
  DIO8
  Copyright (c) 2020 Cyrus Brunner
  www.cyrusbuilt.net
  GND
  CyGate4 - I/O Breakout, CyGate4 I/O Break-out adapter, 1.1
  To CyGate4 Conn J23
  To CyGate4 Conn J11
  SDA
  SCL
  ULN2803A
  I/O Reset
  I/O Reset Lines
  NOTE: RST (IO16) is a shared pin with the ULN2803.
  The RST line is dedicated to providing a reset function to peripherals that need it.
  The ULN2803 is essentially used to multiplex the reset line and provide 8 more reset connections.
